// Digital circuit CPU.dig as structural Verilog
module CPU (
  input  Clock,
  input  [31:0] VemDoIDStage,
  input  [31:0] VemDoEXStage,
  input  [1:0] PCSrc,
  input  PCWrite,
  input  [31:0] IF_ID_Instruction,
  input  [31:0] R_rs1,
  input  [31:0] R_rs2,
  input  [31:0] IF_ID_PC,
  input  [31:0] ImediatoDoImmGen,
  output [31:0] out_2,
  output [31:0] VaiVirarInstMem,
  output [31:0] Imediato,
  output BitIgualdade,
  output [31:0] NextPC_Branch_Jal
);

  wire [31:0] multiplexer_1_out;

  IF_ID #(.applicationType("GHDL")) u_IF_ID ();  // open: rst, clk, IF_ID_WRITE, IF_ID_flush, PC_in, inst_in, PC_out, rs1, rs2, rd, inst_out
  CheckEquality #(.applicationType("GHDL")) u_CheckEquality (.Rs1(R_rs1), .Rs2(R_rs2), .IsEqual(BitIgualdade));
  Multiplexer #(.Bits(32), .Selector_Bits(2)) multiplexer_1 (
    .sel(PCSrc), .in_0(out_2), .in_1(VemDoIDStage), .in_2(VemDoEXStage), .out(multiplexer_1_out));  // open: in_3
  ID_EX #(.applicationType("GHDL")) u_ID_EX ();  // open: rst, clk, rs1_in, rs2_in, rd_in, rs1_data_in, rs2_data_in, immediate_in, EXSignals_in, MEMSignals_in, WBSignals_in, rs1_out, rs2_out, rd_out, rs1_data_out, rs2_data_out, immediate_out, MEMSignals_out, WBSignals_out, ALUSrcA, ALUSrcB, ALUOp
  Register #(.Bits(32)) PC (.D(multiplexer_1_out), .C(Clock), .en(PCWrite), .Q(VaiVirarInstMem));
  PCPlusFour #(.applicationType("GHDL")) u_PCPlusFour (.PC(VaiVirarInstMem), .Next_PC(out_2));
  PCPlusImm #(.applicationType("GHDL")) u_PCPlusImm (
    .PC(IF_ID_PC), .IMM(ImediatoDoImmGen), .Next_PC(NextPC_Branch_Jal));
  EX_MEM #(.applicationType("GHDL")) u_EX_MEM ();  // open: rst, clk, rd_in, rs2_data_in, ALUoutput_in, MEMSignals_in, WBSignals_in, rd_out, rs2_data_out, ALUoutput_out, MemRead, MemWrite, WBSignals_out
  ImmGen #(.applicationType("GHDL")) u_ImmGen (.Instruction(IF_ID_Instruction), .Immediate(Imediato));
  EX_MEM #(.applicationType("GHDL")) u_EX_MEM_2 ();  // open: rst, clk, rd_in, DataFromMem_in, ALUoutput_in, WBSignals_in, rd_out, DataFromMem_out, ALUoutput_out, MemToReg, RegWrite
  // Pins of 1 and 32 bits meet at VaiVirarInstMem
  // Pins of 16 and 32 bits meet at out_2
  // Pins of 1 and 32 bits meet at VemDoIDStage
  // Pins of 1 and 32 bits meet at VemDoEXStage
  // Pins of 1 and 32 bits meet at IF_ID_PC
  // Pins of 1 and 32 bits meet at ImediatoDoImmGen
  // Pins of 1 and 32 bits meet at NextPC_Branch_Jal
endmodule

/* Code of IF_ID:
library IEEE;
use IEEE.STD_LOGIC_1164.ALL;

entity IF_ID is
    Port ( 
	rst     	: in  STD_LOGIC; 
        clk		: in  STD_LOGIC;

	IF_ID_WRITE	: in STD_LOGIC;
	IF_ID_flush	: in STD_LOGIC;
        PC_in		: in  STD_LOGIC_VECTOR(31 downto 0);
        inst_in		: in  STD_LOGIC_VECTOR(31 downto 0);

	PC_out		: out STD_LOGIC_VECTOR(31 downto 0);
        rs1		: out STD_LOGIC_VECTOR(4 downto 0);
        rs2		: out STD_LOGIC_VECTOR(4 downto 0);
	rd		: out STD_LOGIC_VECTOR(4 downto 0);
	inst_out	: out STD_LOGIC_VECTOR(31 downto 0)

    );
end IF_ID;

architecture Behavioral of IF_ID is

signal s_dado : STD_LOGIC_VECTOR(31 downto 0);

begin

process(clk,rst)
begin
	if rst = '1' then
		s_dado <= (others => '0');
        elsif rising_edge(clk) and IF_ID_WRITE='0' then
		if IF_ID_flush='1' then
			PC_out <= (others => '0');
			inst_out <= (others => '0');
		else
			PC_out <= PC_in;
            		inst_out <= inst_in;
		end if;
	end if;
end process;

rs1 <= inst_out(19 downto 15);
rs2 <= inst_out(24 downto 20);
rd <= inst_out(11 downto 7);

end Behavioral;
*/

/* Code of CheckEquality:
library IEEE;
use IEEE.STD_LOGIC_1164.ALL;
use IEEE.NUMERIC_STD.ALL;

entity CheckEquality is
    Port (
        Rs1        : in  STD_LOGIC_VECTOR(31 downto 0);
	Rs2	  : in  STD_LOGIC_VECTOR(31 downto 0);
        IsEqual   : out  STD_LOGIC
    );
end CheckEquality;

architecture Behavioral of CheckEquality is
begin
	IsEqual <= '1' when Rs1 = Rs2 else '0';
end Behavioral;
*/

/* Code of ID_EX:
library IEEE;
use IEEE.STD_LOGIC_1164.ALL;

entity ID_EX is
    Port ( 
	rst     	: in  STD_LOGIC; 
        clk		: in  STD_LOGIC;

        rs1_in		: in  STD_LOGIC_VECTOR(4 downto 0);
        rs2_in		: in  STD_LOGIC_VECTOR(4 downto 0);
        rd_in		: in  STD_LOGIC_VECTOR(4 downto 0);
        rs1_data_in	: in  STD_LOGIC_VECTOR(31 downto 0);
        rs2_data_in	: in  STD_LOGIC_VECTOR(31 downto 0);
        immediate_in	: in  STD_LOGIC_VECTOR(31 downto 0);

        EXSignals_in	: in  STD_LOGIC_VECTOR(4 downto 0);
        MEMSignals_in	: in  STD_LOGIC_VECTOR(31 downto 0);
        WBSignals_in	: in  STD_LOGIC_VECTOR(31 downto 0);

	rs1_out		: out STD_LOGIC_VECTOR(4 downto 0);
	rs2_out		: out STD_LOGIC_VECTOR(4 downto 0);
	rd_out		: out STD_LOGIC_VECTOR(4 downto 0);
        rs1_data_out	: out STD_LOGIC_VECTOR(31 downto 0);
        rs2_data_out	: out STD_LOGIC_VECTOR(31 downto 0);
	immediate_out	: out STD_LOGIC_VECTOR(31 downto 0);


	MEMSignals_out	: out STD_LOGIC_VECTOR(31 downto 0);
	WBSignals_out	: out STD_LOGIC_VECTOR(31 downto 0);
	ALUSrcA		: out STD_LOGIC;
	ALUSrcB		: out STD_LOGIC;
	ALUOp		: out STD_LOGIC_VECTOR(1 downto 0)

    );
end ID_EX;

architecture Behavioral of ID_EX is

signal s_dado : STD_LOGIC_VECTOR(31 downto 0);

begin

process(clk,rst)
begin
	if rst = '1' then
		rs1_out <= (others => '0');
		rs2_out <= (others => '0');
		rd_out <= (others => '0');
		rs1_data_out <= (others => '0');
		rs2_data_out <= (others => '0');
		immediate_out <= (others => '0');
		ALUSrcA <= '0';
		ALUSrcB <= '0';
		ALUOp <= (others => '0');
		MEMSignals_out <= (others => '0');
		WBSignals_out <= (others => '0');
        elsif rising_edge(clk) then
		rs1_out <= rs1_in;
		rs2_out <= rs2_in;
		rd_out <= rd_in;
		rs1_data_out <= rs1_data_in;
		rs2_data_out <= rs2_data_in;
		immediate_out <= immediate_in;
		ALUSrcA <= EXSignals_in(0);
		ALUSrcB <= EXSignals_in(1);
		ALUOp <= EXSignals_in(3 downto 2);
		MEMSignals_out <= MEMSignals_in;
		WBSignals_out <= WBSignals_in;
	end if;
end process;

end Behavioral;
*/

/* Code of PCPlusFour:
library IEEE;
use IEEE.STD_LOGIC_1164.ALL;
use IEEE.NUMERIC_STD.ALL;

entity PCPlusFour is
    Port (
        PC        : in  STD_LOGIC_VECTOR(31 downto 0);
        Next_PC   : out  STD_LOGIC_VECTOR(31 downto 0)
    );
end PCPlusFour;

architecture Behavioral of PCPlusFour is
begin
	Next_PC <= std_logic_vector(unsigned(PC) + 4);
end Behavioral;
*/

/* Code of PCPlusImm:
library IEEE;
use IEEE.STD_LOGIC_1164.ALL;
use IEEE.NUMERIC_STD.ALL;

entity PCPlusImm is
    Port (
        PC        : in  STD_LOGIC_VECTOR(31 downto 0);
	IMM	  : in  STD_LOGIC_VECTOR(31 downto 0);
        Next_PC   : out  STD_LOGIC_VECTOR(31 downto 0)
    );
end PCPlusImm;

architecture Behavioral of PCPlusImm is
begin
	Next_PC <= std_logic_vector(unsigned(PC) + unsigned(IMM));
end Behavioral;
*/

/* Code of EX_MEM:
library IEEE;
use IEEE.STD_LOGIC_1164.ALL;

entity EX_MEM is
    Port ( 
	rst     	: in  STD_LOGIC; 
        clk		: in  STD_LOGIC;

        rd_in		: in  STD_LOGIC_VECTOR(4 downto 0);
        rs2_data_in	: in  STD_LOGIC_VECTOR(31 downto 0); --for store instruction
	ALUoutput_in	: in  STD_LOGIC_VECTOR(31 downto 0);

	MEMSignals_in	: in STD_LOGIC_VECTOR(1 downto 0);
	WBSignals_in	: in STD_LOGIC_VECTOR(1 downto 0);

	rd_out		: out STD_LOGIC_VECTOR(4 downto 0);
        rs2_data_out	: out STD_LOGIC_VECTOR(31 downto 0);
	ALUoutput_out	: out  STD_LOGIC_VECTOR(31 downto 0);

	MemRead		: out STD_LOGIC;
	MemWrite	: out STD_LOGIC;
	WBSignals_out	: out STD_LOGIC_VECTOR(1 downto 0)
    );
end EX_MEM;

architecture Behavioral of EX_MEM is

signal s_dado : STD_LOGIC_VECTOR(31 downto 0);

begin

process(clk,rst)
begin
	if rst = '1' then
		rd_out <= (others => '0');
		rs2_data_out <= (others => '0');
		ALUoutput_out <= (others => '0');
		MemRead <= '0';
		MemWrite <= '0';
		WBSignals_out <= (others => '0');
        elsif rising_edge(clk) then
		rd_out <= rd_in;
		rs2_data_out <= rs2_data_in;
		ALUoutput_out <= ALUoutput_in;
		MemRead <= MEMSignals_in(0);
		MemWrite <= MEMSignals_in(1);
		WBSignals_out <= WBSignals_in;
	end if;
end process;

end Behavioral;
*/

/* Code of ImmGen:
library IEEE;
use IEEE.STD_LOGIC_1164.ALL;
use IEEE.NUMERIC_STD.ALL;

entity ImmGen is
    Port (
        Instruction	: in  STD_LOGIC_VECTOR(31 downto 0);
        Immediate   	: out  STD_LOGIC_VECTOR(31 downto 0)
    );
end ImmGen;

architecture Behavioral of ImmGen is

signal opcode : STD_LOGIC_VECTOR(6 downto 0);

begin

opcode <= Instruction(6 downto 0);

process(opcode)
begin
    case opcode is

        when "0110011" =>
		-- R type
		Immediate <= (others => '0');

        when "0010011" | "1100111" | "0000011" =>
		-- I type
		Immediate <= (others => Instruction (31));
		Immediate (11 downto 0) <= Instruction (31 downto 20);

        when "0010111" | "0110111" => 
            	-- U type
            	Immediate <= (others => '0');
		Immediate (31 downto 12) <= Instruction (31 downto 12);

        when "1100011" => 
            	-- SB type
		Immediate <= (others => Instruction (31));
		Immediate (0) <= '0';
		Immediate (11) <= Instruction (7);
		Immediate (4 downto 1) <= Instruction (11 downto 8);
		Immediate (10 downto 5) <= Instruction (30 downto 25);

        when "1101111" => 
            	-- UJ type
		Immediate <= (others => Instruction (31));
		Immediate (0) <= '0';
		Immediate (11) <= Instruction (20);
		Immediate (19 downto 12) <= Instruction (19 downto 12);
		Immediate (10 downto 1) <= Instruction (30 downto 21);
            	
        when "0100011" => 
           	 -- S type
            	Immediate <= (others => Instruction (31));
		Immediate (11 downto 5) <= Instruction (31 downto 25);
		Immediate (4 downto 0) <= Instruction (11 downto 7);

        when others =>
            	Immediate <= (others => '0');

    end case;
end process;

end Behavioral;
*/

/* Code of EX_MEM:
library IEEE;
use IEEE.STD_LOGIC_1164.ALL;

entity EX_MEM is
    Port ( 
	rst     	: in  STD_LOGIC; 
        clk		: in  STD_LOGIC;

        rd_in		: in  STD_LOGIC_VECTOR(4 downto 0);
        DataFromMem_in	: in  STD_LOGIC_VECTOR(31 downto 0);
	ALUoutput_in	: in  STD_LOGIC_VECTOR(31 downto 0);

	WBSignals_in	: in STD_LOGIC_VECTOR(1 downto 0);

	rd_out		: out STD_LOGIC_VECTOR(4 downto 0);
        DataFromMem_out	: out STD_LOGIC_VECTOR(31 downto 0);
	ALUoutput_out	: out  STD_LOGIC_VECTOR(31 downto 0);

	MemToReg 	: out STD_LOGIC;
	RegWrite 	: out STD_LOGIC
    );
end EX_MEM;

architecture Behavioral of EX_MEM is

signal s_dado : STD_LOGIC_VECTOR(31 downto 0);

begin

process(clk,rst)
begin
	if rst = '1' then
		rd_out <= (others => '0');
		DataFromMem_out <= (others => '0');
		ALUoutput_out <= (others => '0');
		MemToReg <= '0';
		RegWrite <= '0';
        elsif rising_edge(clk) then
		rd_out <= rd_in;
		DataFromMem_out <= DataFromMem_in;
		ALUoutput_out <= ALUoutput_in;
		MemToReg <= WBSignals_in(0);
		RegWrite <= WBSignals_in(1);
	end if;
end process;

end Behavioral;
*/
